// Logisim project CO MS2c.circ as structural Verilog: 3 circuits, main circuit ALU
module ALU (
  input  [15:0] AC,
  input  [15:0] DR,
  input  [3:0] Sel,
  input  E,
  input  [7:0] INPR,
  output [15:0] Output,
  output out_7
);

  wire adder_1_cout, subtractor_1_bout;
  wire [15:0] adder_1_out, and_1_out, bit_extender_1_out, not_1_out, or_1_out, subtractor_1_out, xor_1_out;
  wire [16:0] shifter_1_out, shifter_2_out;

  assign and_1_out = AC & DR;  // AND_Gate and_1, 16 bits wide
  assign bit_extender_1_out = {{8{1'b0}}, INPR};  // Bit_Extender bit_extender_1
  assign or_1_out = AC | DR;  // OR_Gate or_1, 16 bits wide
  Adder #(.width(16)) adder_1 (.a(AC), .b(DR), .out(adder_1_out), .cin(1'b0), .cout(adder_1_cout));
  Subtractor #(.width(16)) subtractor_1 (.a(AC), .b(DR), .out(subtractor_1_out), .bin(1'b0), .bout(subtractor_1_bout));
  assign not_1_out = ~AC;  // NOT_Gate not_1, 16 bits wide
  assign xor_1_out = DR ^ AC;  // XOR_Gate xor_1, 16 bits wide
  Shifter #(.width(17), .shift("rl")) shifter_1 (.in({E, AC}), .\dist (5'b00001), .out(shifter_1_out));
  Shifter #(.width(17), .shift("rr")) shifter_2 (.in({E, AC}), .\dist (5'b00001), .out(shifter_2_out));
  Multiplexer #(.select(4), .width(16)) multiplexer_1 (
    .in0(and_1_out), .in1(or_1_out), .in2(adder_1_out), .in3(subtractor_1_out), .in4(DR), .in5(not_1_out),
    .in6(xor_1_out), .in7(shifter_1_out[15:0]), .in8(shifter_2_out[15:0]), .in9(bit_extender_1_out),
    .out(Output), .sel(Sel), .en(1'b1));  // open: in10, in11, in12, in13, in14, in15
  Multiplexer #(.select(4)) multiplexer_2 (
    .in0(1'b0), .in1(1'b0), .in2(adder_1_cout), .in3(subtractor_1_bout), .in4(1'b0), .in5(1'b0), .in6(1'b0),
    .in7(shifter_1_out[16]), .in8(shifter_2_out[16]), .in9(1'b0), .in10(1'b0), .in11(1'b0), .in12(1'b0),
    .in13(1'b0), .in14(1'b0), .in15(1'b0), .out(out_7), .sel(Sel), .en(1'b1));
endmodule

module Bus_System (
  input  E,
  input  in_2,
  input  in_3,
  input  in_4,
  output [3:0] out_5
);

  wire ACCLR, ACCLR1, ACINCR, ACLD, alu_1_out_7, and_1_out, ARCLR, ARCLR1, ARINCR, ARLD, CLK, DRINCR, DRLD,
       E_J, E_J1, E_K, E_K1, E_t, FGI, FGI_K, FGI_K1, FGO, FGO_K, FGO_K1, I, I_J, IEN, IEN_J, IEN_J1, IEN_K,
       IEN_K1, IRLD, not_1_out, OUTRLD, PCCLR, PCCLR1, PCINCR, PCLD, R, R_J, R_K, READ, S, S0, S1, S2, S_K,
       S_K1, SCCLR, SCCLR1, TRLD, WRITE;
  wire [2:0] Opcode;
  wire [3:0] ALU, OUTR_q;
  wire [6:0] keyboard_1_data;
  wire [7:0] bit_extender_1_out, bit_extender_4_out, INPR_q;
  wire [7:4] OUTR_q_2;
  wire [11:0] AR_q, bit_extender_2_out, bit_extender_3_out, IR, IR_q, PC_q;
  wire [15:0] AC, alu_1_output, bit_extender_5_out, bit_extender_6_out, DR, multiplexer_1_out, ram_1_data,
       TR_q;

  Keyboard #(.buflen(64)) keyboard_1 (.clk(CLK), .re(FGI), .data(keyboard_1_data));  // open: clr, avail
  Hex_Digit_Display hex_digit_display_1 (.value(OUTR_q_2));  // open: dp
  Clock clock_1 (.out(CLK));
  Hex_Digit_Display hex_digit_display_2 (.value(OUTR_q));  // open: dp
  D_Flip_Flop d_ff_1 (.clk(CLK), .D(SCCLR), .Q(SCCLR1), .preset(1'b0), .en(1'b1), .reset(1'b0));  // open: Qn
  D_Flip_Flop d_ff_2 (.clk(CLK), .D(ARCLR), .Q(ARCLR1), .preset(1'b0), .en(1'b1), .reset(1'b0));  // open: Qn
  assign bit_extender_1_out = {{1{1'b0}}, keyboard_1_data};  // Bit_Extender bit_extender_1
  D_Flip_Flop u_FGI (.clk(CLK), .Q(FGI), .en(1'b1), .reset(FGI_K1));  // open: D, Qn, preset
  J_K_Flip_Flop u_R (.J(R_J), .clk(CLK), .K(R_K), .Q(R), .preset(1'b0), .en(1'b1), .reset(1'b0));  // open: Qn
  D_Flip_Flop d_ff_3 (.clk(CLK), .D(ACCLR), .Q(ACCLR1), .preset(1'b0), .en(1'b1), .reset(1'b0));  // open: Qn
  D_Flip_Flop d_ff_4 (.clk(CLK), .D(PCCLR), .Q(PCCLR1), .preset(1'b0), .en(1'b1), .reset(1'b0));  // open: Qn
  D_Flip_Flop d_ff_5 (.clk(CLK), .D(E_J), .Q(E_J1));  // open: Qn, preset, en, reset
  D_Flip_Flop d_ff_6 (.clk(CLK), .D(E_K), .Q(E_K1));  // open: Qn, preset, en, reset
  D_Flip_Flop d_ff_7 (.clk(CLK), .D(IEN_J), .Q(IEN_J1));  // open: Qn, preset, en, reset
  D_Flip_Flop d_ff_8 (.clk(CLK), .D(IEN_K), .Q(IEN_K1));  // open: Qn, preset, en, reset
  Counter INPR (.D(bit_extender_1_out), .count(1'b0), .Q(INPR_q), .clr(1'b0));  // open: load, carry, clk
  D_Flip_Flop d_ff_9 (.clk(CLK), .Q(FGO), .en(1'b1), .reset(FGO_K1));  // open: D, Qn, preset
  Bit_Extender #(.in_width(16), .out_width(12)) bit_extender_2 (.in(multiplexer_1_out), .out(bit_extender_2_out));
  Bit_Extender #(.in_width(16), .out_width(12)) bit_extender_3 (.in(multiplexer_1_out), .out(bit_extender_3_out));
  ALU alu_1 (.AC(AC), .DR(DR), .E(E_t), .INPR(INPR_q), .Sel(ALU), .Output(alu_1_output), .out_7(alu_1_out_7));
  Bit_Extender #(.in_width(16), .out_width(8)) bit_extender_4 (.in(multiplexer_1_out), .out(bit_extender_4_out));
  not not_1 (not_1_out, SCCLR1);
  D_Flip_Flop d_ff_10 (.clk(CLK), .D(alu_1_out_7), .Q(E_t), .preset(E_J1), .en(1'b1), .reset(E_J1));  // open: Qn
  Counter OUTR (
    .load(in_2), .D(bit_extender_4_out), .count(1'b0), .Q({OUTR_q_2, OUTR_q}), .clk(CLK), .clr(1'b0));  // open: carry
  and and_1 (and_1_out, S, not_1_out);
  D_Flip_Flop d_ff_11 (.clk(CLK), .Q(S), .en(1'b1), .reset(S_K1));  // open: D, Qn, preset
  D_Flip_Flop d_ff_12 (.clk(CLK), .D(FGI_K), .Q(FGI_K1));  // open: Qn, preset, en, reset
  D_Flip_Flop d_ff_13 (.clk(CLK), .D(FGO_K), .Q(FGO_K1));  // open: Qn, preset, en, reset
  D_Flip_Flop d_ff_14 (.clk(CLK), .D(S_K), .Q(S_K1));  // open: Qn, preset, en, reset
  Counter #(.width(12), .max('hfff)) AR (
    .load(ARLD), .D(bit_extender_2_out), .count(ARINCR), .Q(AR_q), .clk(CLK), .clr(ARCLR1));  // open: carry
  Counter #(.width(12), .max('hfff)) PC (
    .load(PCLD), .D(bit_extender_3_out), .count(PCINCR), .Q(PC_q), .clk(CLK), .clr(PCCLR1));  // open: carry
  Counter #(.width(16), .max('hffff)) u_DR (
    .load(DRLD), .D(multiplexer_1_out), .count(DRINCR), .Q(DR), .clk(CLK), .clr(E));  // open: carry
  Counter #(.width(16), .max('hffff)) u_AC (
    .load(ACLD), .D(alu_1_output), .count(ACINCR), .Q(AC), .clk(CLK), .clr(ACCLR1));  // open: carry
  Counter #(.width(16), .max('hffff)) TR (
    .D(multiplexer_1_out), .count(in_4), .Q(TR_q), .clk(CLK), .clr(in_3));  // open: load, carry
  D_Flip_Flop d_ff_15 (.clk(CLK), .Q(IEN), .preset(IEN_J1), .en(1'b1), .reset(IEN_K1));  // open: D, Qn
  LCU lcu_1 (
    .I(I), .Opcode(Opcode), .SC(out_5), .IR(IR), .DR(DR), .AC(AC), .E(E_t), .R(R), .FGO(FGO), .FGI(FGI),
    .IEN(IEN), .PCINCR(PCINCR), .PCLD(PCLD), .PCCLR(PCCLR), .ARLD(ARLD), .ARCLR(ARCLR), .SCCLR(SCCLR),
    .ARINCR(ARINCR), .READ(READ), .WRITE(WRITE), .S_K(S_K), .IRLD(IRLD), .FGI_K(FGI_K), .FGO_K(FGO_K),
    .E_J(E_J), .E_K(E_K), .IEN_J(IEN_J), .IEN_K(IEN_K), .DRLD(DRLD), .DRINCR(DRINCR), .TRLD(TRLD), .I_J(I_J),
    .OUTRLD(OUTRLD), .R_J(R_J), .R_K(R_K), .S0(S0), .S1(S1), .S2(S2), .ACLD(ACLD), .ACINCR(ACINCR),
    .ACCLR(ACCLR), .ALU(ALU));
  RAM #(.addrWidth(12), .dataWidth(16), .bus("separate")) ram_1 (
    .addr(AR_q), .din(multiplexer_1_out), .data(ram_1_data), .str(WRITE), .sel(1'b1), .clk(CLK), .ld(READ),
    .clr(1'b0));
  Counter #(.width(16), .max('hffff)) u_IR (
    .load(IRLD), .D(multiplexer_1_out), .count(1'b0), .Q({I, Opcode, IR_q}), .clk(CLK), .clr(1'b0));  // open: carry
  Counter #(.width(4), .max('hf)) SC (
    .load(1'b0), .count(and_1_out), .Q(out_5), .clk(CLK), .clr(SCCLR1));  // open: D, carry
  assign bit_extender_5_out = {{4{1'b0}}, AR_q};  // Bit_Extender bit_extender_5
  assign bit_extender_6_out = {{4{1'b0}}, PC_q};  // Bit_Extender bit_extender_6
  Multiplexer #(.select(3), .width(16)) multiplexer_1 (
    .in1(bit_extender_5_out), .in2(bit_extender_6_out), .in3(DR), .in4(AC), .in5({I, Opcode, IR_q}),
    .in6(TR_q), .in7(ram_1_data), .out(multiplexer_1_out), .sel({S2, S1, S0}), .en(1'b1));  // open: in0

  // Other names for the same wires on the sheet: SC[3:0] = out_5
endmodule

module LCU (
  input  I,
  input  [2:0] Opcode,
  input  [3:0] SC,
  input  [11:0] IR,
  input  [15:0] DR,
  input  [15:0] AC,
  input  E,
  input  R,
  input  FGO,
  input  FGI,
  input  IEN,
  output PCINCR,
  output PCLD,
  output PCCLR,
  output ARLD,
  output ARCLR,
  output SCCLR,
  output ARINCR,
  output READ,
  output WRITE,
  output S_K,
  output IRLD,
  output FGI_K,
  output FGO_K,
  output E_J,
  output E_K,
  output IEN_J,
  output IEN_K,
  output DRLD,
  output DRINCR,
  output TRLD,
  output I_J,
  output OUTRLD,
  output R_J,
  output R_K,
  output S0,
  output S1,
  output S2,
  output ACLD,
  output ACINCR,
  output ACCLR,
  output [3:0] ALU
);

  wire and_2_out, and_3_out, and_4_out, and_5_out, and_6_out, and_7_out, and_8_out, and_14_out, and_15_out,
       and_16_out, and_17_out, and_21_out, and_22_out, and_23_out, and_24_out, and_25_out, and_26_out,
       and_27_out, and_28_out, and_30_out, and_31_out, and_32_out, and_33_out, and_34_out, and_35_out,
       and_36_out, and_37_out, and_38_out, and_39_out, and_40_out, and_41_out, and_42_out, and_43_out,
       and_44_out, and_45_out, and_47_out, and_48_out, and_49_out, and_50_out, and_52_out, and_53_out,
       and_54_out, and_55_out, and_61_out, and_62_out, and_63_out, and_64_out, and_65_out, and_66_out,
       and_68_out, and_69_out, and_70_out, and_72_out, and_73_out, and_74_out, D0, D1, D2, D3, D4, D5, D6,
       D7, nor_1_out, not_3_out, not_4_out, not_5_out, not_6_out, not_7_out, not_8_out, not_9_out,
       not_10_out, not_11_out, not_12_out, not_13_out, not_14_out, not_15_out, not_16_out, or_1_out,
       or_2_out, or_3_out, or_4_out, or_5_out, or_8_out, or_9_out, or_13_out, or_21_out, or_22_out, P, RR,
       T0, T1, T2, T3, T4, T5, T6, T7, T8, T9, T10, T11, T12, T13, T14, T15, X1, X2, X3, X4, X5, X6, X7, ZAC,
       ZDR;

  nor nor_1 (nor_1_out, T0, T1, T2);
  or or_1 (or_1_out, FGI, FGO);
  and and_1 (DRINCR, D6, T5);
  or or_2 (or_2_out, D0, D1, D2, D6);
  and and_2 (and_2_out, D0, T5);
  and and_3 (and_3_out, T5, D1);
  and and_4 (and_4_out, T5, D2);
  and and_5 (and_5_out, RR, IR[9]);
  and and_6 (and_6_out, RR, IR[7]);
  and and_7 (and_7_out, RR, IR[6]);
  and and_8 (and_8_out, P, IR[11]);
  and and_9 (R_J, nor_1_out, IEN, or_1_out);
  and and_10 (DRLD, T4, or_2_out);
  Decoder #(.select(3)) decoder_1 (
    .out0(D0), .out1(D1), .out2(D2), .out3(D3), .out4(D4), .out5(D5), .out6(D6), .out7(D7), .sel(Opcode),
    .en(1'b1));
  Decoder #(.select(4)) decoder_2 (
    .out0(T0), .out1(T1), .out2(T2), .out3(T3), .out4(T4), .out5(T5), .out6(T6), .out7(T7), .out8(T8),
    .out9(T9), .out10(T10), .out11(T11), .out12(T12), .out13(T13), .out14(T14), .out15(T15), .sel(SC),
    .en(1'b1));
  or or_3 (or_3_out, DR[0], DR[1], DR[2], DR[3], DR[4], DR[5], DR[6], DR[7], DR[8], DR[9], DR[10], DR[11], DR[12], DR[13], DR[14], DR[15]);
  or or_4 (or_4_out, AC[0], AC[1], AC[2], AC[3], AC[4], AC[5], AC[6], AC[7], AC[8], AC[9], AC[10], AC[11], AC[12], AC[13], AC[14], AC[15]);
  and and_11 (R_K, R, T2);
  not not_1 (ZDR, or_3_out);
  not not_2 (ZAC, or_4_out);
  and and_12 (P, I, D7, T3);
  and and_13 (TRLD, T0, R);
  Priority_Encoder #(.select(4)) priority_encoder_1 (
    .in0(and_2_out), .in2(and_3_out), .in4(and_4_out), .in5(and_5_out), .in7(and_6_out), .in8(and_7_out),
    .in9(and_8_out), .out(ALU), .en_in(1'b1));  // open: in1, in3, in6, in10, in11, in12, in13, in14, in15, gs, en_out
  not not_3 (not_3_out, E);
  not not_4 (not_4_out, R);
  and and_14 (and_14_out, IR[8], not_3_out);
  not not_5 (not_5_out, R);
  and and_15 (and_15_out, D5, T4);
  and and_16 (and_16_out, D4, T4);
  and and_17 (and_17_out, D5, T5);
  not not_6 (not_6_out, I);
  not not_7 (not_7_out, AC[15]);
  not not_8 (not_8_out, E);
  and and_18 (IRLD, not_4_out, T1);
  or or_5 (or_5_out, and_14_out, IR[7], IR[6], IR[5]);
  and and_19 (X6, R, T1);
  and and_20 (X5, not_5_out, T2);
  or or_6 (X2, T0, and_15_out);
  or or_7 (X1, and_16_out, and_17_out);
  and and_21 (and_21_out, D1, T5);
  and and_22 (and_22_out, RR, or_5_out);
  and and_23 (and_23_out, IR[10], RR);
  and and_24 (and_24_out, RR, E, IR[8]);
  or or_8 (or_8_out, D3, D4);
  and and_25 (and_25_out, D7, T3);
  or or_9 (or_9_out, D0, D1, D2, D5);
  and and_26 (and_26_out, D6, T6);
  and and_27 (and_27_out, D4, T4);
  and and_28 (and_28_out, D5, T5);
  and and_29 (RR, D7, not_6_out, T3);
  and and_30 (and_30_out, D6, ZDR, T6);
  and and_31 (and_31_out, RR, IR[4], not_7_out);
  and and_32 (and_32_out, AC[15], RR, IR[3]);
  and and_33 (and_33_out, RR, IR[2], ZAC);
  and and_34 (and_34_out, RR, IR[1], not_8_out);
  and and_35 (and_35_out, IR[8], FGO, P);
  and and_36 (and_36_out, P, FGI, IR[9]);
  not not_9 (not_9_out, R);
  and and_37 (and_37_out, not_9_out, T1);
  or or_10 (E_J, and_21_out, and_22_out);
  or or_11 (E_K, and_23_out, and_24_out);
  and and_38 (and_38_out, T4, or_8_out);
  and and_39 (and_39_out, R, T2);
  or or_12 (PCLD, and_27_out, and_28_out);
  or or_13 (or_13_out, D0, D1, D2, D6);
  not not_10 (not_10_out, D7);
  not not_11 (not_11_out, R);
  and and_40 (and_40_out, D2, T5);
  and and_41 (and_41_out, D6, T6);
  and and_42 (and_42_out, D3, T4);
  and and_43 (and_43_out, P, IR[10]);
  and and_44 (and_44_out, or_9_out, T5);
  and and_45 (and_45_out, R, T2);
  and and_46 (S_K, RR, IR[0]);
  and and_47 (and_47_out, or_13_out, T4);
  and and_48 (and_48_out, T3, not_10_out, I);
  and and_49 (and_49_out, T1, not_11_out);
  or or_14 (SCCLR, and_38_out, and_25_out, and_39_out, and_44_out, and_26_out);
  not not_12 (not_12_out, R);
  or or_15 (PCINCR, and_30_out, and_31_out, and_32_out, and_33_out, and_34_out, and_35_out, and_36_out, and_37_out, and_45_out);
  or or_16 (X7, and_47_out, and_48_out, and_49_out);
  or or_17 (X3, and_40_out, and_41_out);
  or or_18 (X4, and_42_out, and_43_out);
  and and_50 (and_50_out, T2, not_12_out);
  and and_51 (OUTRLD, IR[10], P);
  not not_13 (not_13_out, D7);
  and and_52 (and_52_out, not_13_out, I, T3);
  and and_53 (and_53_out, T0, not_12_out);
  and and_54 (and_54_out, P, IR[6]);
  and and_55 (and_55_out, R, T2);
  and and_56 (ARCLR, T0, R);
  and and_57 (ARINCR, D5, T4);
  or or_19 (ARLD, and_52_out, and_50_out, and_53_out);
  and and_58 (PCCLR, T1, R);
  not not_14 (not_14_out, D7);
  and and_59 (IEN_J, P, IR[7]);
  or or_20 (IEN_K, and_54_out, and_55_out);
  not not_15 (not_15_out, R);
  or or_21 (or_21_out, D0, D1, D2, D6);
  or or_22 (or_22_out, D3, D5);
  and and_60 (FGO_K, P, IR[10]);
  and and_61 (and_61_out, I, not_14_out, T3);
  and and_62 (and_62_out, T1, not_15_out);
  and and_63 (and_63_out, T4, or_21_out);
  and and_64 (and_64_out, R, T1);
  and and_65 (and_65_out, T4, or_22_out);
  and and_66 (and_66_out, D6, T6);
  and and_67 (FGI_K, IR[11], P);
  not not_16 (not_16_out, R);
  and and_68 (and_68_out, T5, D0);
  and and_69 (and_69_out, T5, D1);
  and and_70 (and_70_out, D2, T5);
  // AND_Gate and_71 has open pins: in0=P, in1=IR[11], out=open
  and and_72 (and_72_out, RR, IR[9]);
  and and_73 (and_73_out, RR, IR[7]);
  and and_74 (and_74_out, RR, IR[6]);
  and and_75 (ACINCR, RR, IR[5]);
  and and_76 (ACCLR, RR, IR[11]);
  or or_23 (READ, and_61_out, and_62_out, and_63_out);
  or or_24 (WRITE, and_64_out, and_65_out, and_66_out);
  and and_77 (I_J, not_16_out, T2);
  or or_25 (ACLD, and_68_out, and_69_out, and_70_out, and_72_out, and_73_out, and_74_out);
  or or_26 (S0, X1, X3, X5, X7);
  or or_27 (S1, X2, X3, X6, X7);
  or or_28 (S2, X4, X6, X5, X7);

  // Other names for the same wires on the sheet: B0 = IR[0]; B1 = IR[1]; B2 = IR[2]; B3 = IR[3]; B4 = IR[4];
  //   B5 = IR[5]; B6 = IR[6]; B7 = IR[7]; B8 = IR[8]; B9 = IR[9]; B10 = IR[10]; B11 = IR[11]
endmodule
