// Logisim project Milestone 1.circ as structural Verilog: 2 circuits, main circuit main
module main (
  input  in_1,
  input  in_2,
  input  in_3,
  input  in_4,
  input  AR,
  input  in_6,
  input  PC,
  input  in_8,
  input  in_9,
  input  [2:0] in_10,
  input  DR,
  input  in_12,
  input  in_13,
  input  AC,
  input  in_15,
  input  [3:0] in_16,
  input  in_17,
  input  in_18,
  input  IR,
  input  in_20,
  input  in_21,
  input  TR,
  input  in_23
);

  wire alu_1_carry, clock_1_out;
  wire [7:0] bit_extender_3_out, register_1_q;
  wire [11:0] bit_extender_1_out, bit_extender_2_out, counter_1_q, counter_2_q;
  wire [15:0] alu_1_output, bit_extender_4_out, bit_extender_5_out, counter_3_q, counter_4_q, counter_5_q,
       multiplexer_1_out, ram_1_data, register_2_q;

  Bit_Extender #(.in_width(16), .out_width(12)) bit_extender_1 (.in(multiplexer_1_out), .out(bit_extender_1_out));
  Bit_Extender #(.in_width(16), .out_width(12)) bit_extender_2 (.in(multiplexer_1_out), .out(bit_extender_2_out));
  ALU alu_1 (
    .DR(counter_3_q), .AC(counter_4_q), .Select(in_16), .INPR(register_1_q), .Output(alu_1_output),
    .Carry(alu_1_carry));
  Register register_1 (.Q(register_1_q), .clk(clock_1_out));  // open: D, en, clr
  Bit_Extender #(.in_width(16), .out_width(8)) bit_extender_3 (.in(multiplexer_1_out), .out(bit_extender_3_out));
  Counter #(.width(12), .max('hfff)) counter_1 (
    .load(in_4), .D(bit_extender_1_out), .count(AR), .Q(counter_1_q), .clk(clock_1_out), .clr(in_6));  // open: carry
  Counter #(.width(12), .max('hfff)) counter_2 (
    .load(PC), .D(bit_extender_2_out), .count(in_8), .Q(counter_2_q), .clk(clock_1_out), .clr(in_9));  // open: carry
  Counter #(.width(16), .max('hffff)) counter_3 (
    .load(DR), .D(multiplexer_1_out), .count(in_12), .Q(counter_3_q), .clk(clock_1_out), .clr(in_13));  // open: carry
  Counter #(.width(16), .max('hffff)) counter_4 (
    .load(AC), .D(alu_1_output), .count(in_15), .Q(counter_4_q), .clk(clock_1_out), .clr(in_17));  // open: carry
  Register #(.width(16)) register_2 (.D(multiplexer_1_out), .en(in_18), .Q(register_2_q), .clk(clock_1_out), .clr(IR));
  Counter #(.width(16), .max('hffff)) counter_5 (
    .load(in_20), .D(multiplexer_1_out), .count(in_21), .Q(counter_5_q), .clk(clock_1_out), .clr(TR));  // open: carry
  Counter counter_6 (.load(in_23), .D(bit_extender_3_out), .clk(clock_1_out));  // open: count, Q, carry, clr
  RAM #(.addrWidth(12), .dataWidth(16), .bus("separate")) ram_1 (
    .addr(counter_1_q), .din(multiplexer_1_out), .data(ram_1_data), .str(in_1), .clk(clock_1_out), .ld(in_2),
    .clr(in_3));  // open: sel
  assign bit_extender_4_out = {{4{1'b0}}, counter_1_q};  // Bit_Extender bit_extender_4
  assign bit_extender_5_out = {{4{1'b0}}, counter_2_q};  // Bit_Extender bit_extender_5
  D_Flip_Flop d_ff_1 (.clk(clock_1_out), .D(alu_1_carry));  // open: Q, Qn, preset, en, reset
  Clock clock_1 (.out(clock_1_out));
  Multiplexer #(.select(3), .width(16), .enable("false")) multiplexer_1 (
    .in1(bit_extender_4_out), .in2(bit_extender_5_out), .in3(counter_3_q), .in4(counter_4_q),
    .in5(register_2_q), .in6(counter_5_q), .in7(ram_1_data), .out(multiplexer_1_out), .sel(in_10));  // open: in0

  // Notes on the sheet:
  //   ALU
  //   INPR
  //   OUTR
  //   E
endmodule

module ALU (
  input  [15:0] DR,
  input  [15:0] AC,
  input  [7:0] INPR,
  input  [3:0] Select,
  output [15:0] Output,
  output Carry
);

  wire adder_1_cout, adder_2_cout;
  wire [15:0] adder_1_out, adder_2_out, and_1_out, bit_extender_1_out, not_1_out, not_2_out, or_1_out,
       shifter_1_out, shifter_2_out, xor_1_out;

  assign bit_extender_1_out = {{8{1'b0}}, INPR};  // Bit_Extender bit_extender_1
  assign xor_1_out = DR ^ AC;  // XOR_Gate xor_1, 16 bits wide
  assign not_1_out = ~DR;  // NOT_Gate not_1, 16 bits wide
  Shifter #(.width(16)) shifter_1 (.in(AC), .\dist (4'b0001), .out(shifter_1_out));
  Shifter #(.width(16), .shift("lr")) shifter_2 (.in(AC), .\dist (4'b0001), .out(shifter_2_out));
  assign and_1_out = DR & AC;  // AND_Gate and_1, 16 bits wide
  assign or_1_out = DR | AC;  // OR_Gate or_1, 16 bits wide
  Adder #(.width(16)) adder_1 (.a(DR), .b(AC), .out(adder_1_out), .cin(1'b0), .cout(adder_1_cout));
  Adder #(.width(16)) adder_2 (.a(not_1_out), .b(AC), .out(adder_2_out), .cin(1'b1), .cout(adder_2_cout));
  assign not_2_out = ~AC;  // NOT_Gate not_2, 16 bits wide
  Multiplexer #(.enable("false")) multiplexer_1 (.in0(adder_1_cout), .in1(adder_2_cout), .out(Carry), .sel(Select[0]));
  Multiplexer #(.select(4), .width(16)) multiplexer_2 (
    .in0(and_1_out), .in1(or_1_out), .in2(adder_1_out), .in3(adder_2_out), .in4(DR), .in5(not_2_out),
    .in6(xor_1_out), .in7(shifter_1_out), .in8(shifter_2_out), .in9(bit_extender_1_out), .out(Output),
    .sel(Select));  // open: in10, in11, in12, in13, in14, in15, en
endmodule
